// Logisim project project.circ as structural Verilog: 5 circuits, main circuit main
module main (
  input  Player_selector
);

  wire bcc_1_turn, bcc_2_turn, bcc_3_turn, bcc_4_turn, bcc_5_turn, bcc_6_turn, bcc_7_turn, bcc_8_turn,
       bcc_9_turn, button_1_out, button_2_out, button_3_out, button_4_out, button_5_out, button_6_out,
       button_7_out, button_8_out, button_9_out, cdm_8_mark5_1_data_inst, Cl, Code, data, I_Osel,
       In_out_prime, mem, nand_1_out, not_1_out, not_2_out, RAM, tc, win_1_o_win, win_1_tie, win_1_x_win;
  wire [3:0] dm_1__1_out, dm_1__2_out, dm_1__3_out, dm_1__4_out, dm_2__1_out, dm_2__2_out, dm_2__3_out,
       dm_2__4_out, dm_3__1_out, dm_3__2_out, dm_3__3_out, dm_3__4_out, dm_4__1_out, dm_4__2_out,
       dm_4__3_out, dm_4__4_out, dm_5__1_out, dm_5__2_out, dm_5__3_out, dm_5__4_out, dm_6__1_out,
       dm_6__2_out, dm_6__3_out, dm_6__4_out, dm_7__1_out, dm_7__2_out, dm_7__3_out, dm_7__4_out,
       dm_8__1_out, dm_8__2_out, dm_8__3_out, dm_8__4_out, dm_9__1_out, dm_9__2_out, dm_9__3_out,
       dm_9__4_out, I_Oadr, p1, p2, p3, p4, p5, p6, p7, p8, p9;
  wire [7:0] cdm_8_mark5_1_data_out, cdm_8_mark5_1_pc, cdm_8_mark5_1_ps, cdm_8_mark5_1_r0, cdm_8_mark5_1_r2,
       cdm_8_mark5_1_r3, cdm_8_mark5_1_sp, controlled_buffer_1_out, I_Odat;
  wire [7:4] cdm_8_mark5_1_addr;

  LED O_win (.in(win_1_o_win));
  LED X_win (.in(win_1_x_win));
  LED Tie (.in(win_1_tie));
  win win_1 (
    ._1_in(p1), ._2_in(p2), ._3_in(p3), ._4_in(p4), ._5_in(p5), ._6_in(p6), ._7_in(p7), ._8_in(p8),
    ._9_in(p9), .O_win(win_1_o_win), .X_win(win_1_x_win), .Tie(win_1_tie), .Trun_controll(tc));
  // Probe on cdm_8_mark5_1_r0
  // Probe on cdm_8_mark5_1_r0
  and and_1 (I_Osel, not_1_out, Cl, data);
  // Probe on cdm_8_mark5_1_r2
  // Probe on cdm_8_mark5_1_pc
  // Probe on cdm_8_mark5_1_r3
  Clock clock_1 (.out(Cl));
  not not_1 (not_1_out, nand_1_out);
  and and_2 (RAM, nand_1_out, data);
  // Probe on cdm_8_mark5_1_sp
  // Probe on cdm_8_mark5_1_ps
  CdM_8_mark5 cdm_8_mark5_1 (
    .addr({cdm_8_mark5_1_addr, I_Oadr}), .mem_read(In_out_prime), .mem_cycle(mem),
    .data_inst(cdm_8_mark5_1_data_inst), .data_out(cdm_8_mark5_1_data_out),
    .data_in(controlled_buffer_1_out), .r0(cdm_8_mark5_1_r0), .r1(cdm_8_mark5_1_r0), .r2(cdm_8_mark5_1_r2),
    .r3(cdm_8_mark5_1_r3), .PC(cdm_8_mark5_1_pc), .SP(cdm_8_mark5_1_sp), .PS(cdm_8_mark5_1_ps));  // open: clock, IAck, IRQ, vec, reset
  nand nand_1 (nand_1_out, cdm_8_mark5_1_addr[4], cdm_8_mark5_1_addr[5], cdm_8_mark5_1_addr[6], cdm_8_mark5_1_addr[7]);
  DM dm_1 (
    .Player(Player_selector), .Turn(bcc_1_turn), ._1_out(dm_1__1_out), ._2_out(dm_1__2_out),
    ._3_out(dm_1__3_out), ._4_out(dm_1__4_out), .player_out(p1));
  DotMatrix #(.inputtype("row"), .matrixcols(4), .matrixrows(4)) dotmatrix_1 (
    .row0(dm_1__1_out), .row1(dm_1__2_out), .row2(dm_1__3_out), .row3(dm_1__4_out));
  bcc bcc_1 (.can_turn__0_can_1_can_t(tc), .btn(button_1_out), .turn(bcc_1_turn));
  Button button_1 (.out(button_1_out));
  DM dm_2 (
    .Player(Player_selector), .Turn(bcc_2_turn), ._1_out(dm_2__1_out), ._2_out(dm_2__2_out),
    ._3_out(dm_2__3_out), ._4_out(dm_2__4_out), .player_out(p4));
  DotMatrix #(.inputtype("row"), .matrixcols(4), .matrixrows(4)) dotmatrix_2 (
    .row0(dm_2__1_out), .row1(dm_2__2_out), .row2(dm_2__3_out), .row3(dm_2__4_out));
  Button button_2 (.out(button_2_out));
  bcc bcc_2 (.can_turn__0_can_1_can_t(tc), .btn(button_2_out), .turn(bcc_2_turn));
  DM dm_3 (
    .Player(Player_selector), .Turn(bcc_3_turn), ._1_out(dm_3__1_out), ._2_out(dm_3__2_out),
    ._3_out(dm_3__3_out), ._4_out(dm_3__4_out), .player_out(p7));
  DotMatrix #(.inputtype("row"), .matrixcols(4), .matrixrows(4)) dotmatrix_3 (
    .row0(dm_3__1_out), .row1(dm_3__2_out), .row2(dm_3__3_out), .row3(dm_3__4_out));
  bcc bcc_3 (.can_turn__0_can_1_can_t(tc), .btn(button_3_out), .turn(bcc_3_turn));
  Button button_3 (.out(button_3_out));
  assign controlled_buffer_1_out = In_out_prime ? I_Odat : 8'bz;  // Controlled_Buffer controlled_buffer_1
  bcc bcc_4 (.can_turn__0_can_1_can_t(tc), .btn(button_4_out), .turn(bcc_4_turn));
  Button button_4 (.out(button_4_out));
  Button button_5 (.out(button_5_out));
  bcc bcc_5 (.can_turn__0_can_1_can_t(tc), .btn(button_5_out), .turn(bcc_5_turn));
  bcc bcc_6 (.can_turn__0_can_1_can_t(tc), .btn(button_6_out), .turn(bcc_6_turn));
  Button button_6 (.out(button_6_out));
  Decoder #(.disabled(0)) decoder_1 (.out0(Code), .out1(data), .sel(cdm_8_mark5_1_data_inst), .en(mem));
  assign I_Odat = not_2_out ? cdm_8_mark5_1_data_out : 8'bz;  // Controlled_Buffer controlled_buffer_2
  not not_2 (not_2_out, In_out_prime);
  DM dm_4 (
    .Player(Player_selector), .Turn(bcc_4_turn), ._1_out(dm_4__1_out), ._2_out(dm_4__2_out),
    ._3_out(dm_4__3_out), ._4_out(dm_4__4_out), .player_out(p2));
  DotMatrix #(.inputtype("row"), .matrixcols(4), .matrixrows(4)) dotmatrix_4 (
    .row0(dm_4__1_out), .row1(dm_4__2_out), .row2(dm_4__3_out), .row3(dm_4__4_out));
  Button button_7 (.out(button_7_out));
  DM dm_5 (
    .Player(Player_selector), .Turn(bcc_5_turn), ._1_out(dm_5__1_out), ._2_out(dm_5__2_out),
    ._3_out(dm_5__3_out), ._4_out(dm_5__4_out), .player_out(p5));
  DotMatrix #(.inputtype("row"), .matrixcols(4), .matrixrows(4)) dotmatrix_5 (
    .row0(dm_5__1_out), .row1(dm_5__2_out), .row2(dm_5__3_out), .row3(dm_5__4_out));
  Button button_8 (.out(button_8_out));
  DotMatrix #(.inputtype("row"), .matrixcols(4), .matrixrows(4)) dotmatrix_6 (
    .row0(dm_6__1_out), .row1(dm_6__2_out), .row2(dm_6__3_out), .row3(dm_6__4_out));
  DM dm_6 (
    .Player(Player_selector), .Turn(bcc_6_turn), ._1_out(dm_6__1_out), ._2_out(dm_6__2_out),
    ._3_out(dm_6__3_out), ._4_out(dm_6__4_out), .player_out(p8));
  Button button_9 (.out(button_9_out));
  Pull_Resistor pull_resistor_1 (.node(I_Oadr[0]));
  Pull_Resistor pull_resistor_2 (.node(I_Oadr[1]));
  Pull_Resistor pull_resistor_3 (.node(I_Oadr[2]));
  Pull_Resistor pull_resistor_4 (.node(I_Oadr[3]));
  Pull_Resistor pull_resistor_5 (.node(cdm_8_mark5_1_addr[4]));
  Pull_Resistor pull_resistor_6 (.node(cdm_8_mark5_1_addr[5]));
  Pull_Resistor pull_resistor_7 (.node(cdm_8_mark5_1_addr[6]));
  Pull_Resistor pull_resistor_8 (.node(cdm_8_mark5_1_addr[7]));
  DotMatrix #(.inputtype("row"), .matrixcols(4), .matrixrows(4)) dotmatrix_7 (
    .row0(dm_7__1_out), .row1(dm_7__2_out), .row2(dm_7__3_out), .row3(dm_7__4_out));
  DM dm_7 (
    .Player(Player_selector), .Turn(bcc_7_turn), ._1_out(dm_7__1_out), ._2_out(dm_7__2_out),
    ._3_out(dm_7__3_out), ._4_out(dm_7__4_out), .player_out(p3));
  bcc bcc_7 (.can_turn__0_can_1_can_t(tc), .btn(button_7_out), .turn(bcc_7_turn));
  DotMatrix #(.inputtype("row"), .matrixcols(4), .matrixrows(4)) dotmatrix_8 (
    .row0(dm_8__1_out), .row1(dm_8__2_out), .row2(dm_8__3_out), .row3(dm_8__4_out));
  DM dm_8 (
    .Player(Player_selector), .Turn(bcc_8_turn), ._1_out(dm_8__1_out), ._2_out(dm_8__2_out),
    ._3_out(dm_8__3_out), ._4_out(dm_8__4_out), .player_out(p6));
  bcc bcc_8 (.can_turn__0_can_1_can_t(tc), .btn(button_8_out), .turn(bcc_8_turn));
  DM dm_9 (
    .Player(Player_selector), .Turn(bcc_9_turn), ._1_out(dm_9__1_out), ._2_out(dm_9__2_out),
    ._3_out(dm_9__3_out), ._4_out(dm_9__4_out), .player_out(p9));
  DotMatrix #(.inputtype("row"), .matrixcols(4), .matrixrows(4)) dotmatrix_9 (
    .row0(dm_9__1_out), .row1(dm_9__2_out), .row2(dm_9__3_out), .row3(dm_9__4_out));
  bcc bcc_9 (.can_turn__0_can_1_can_t(tc), .btn(button_9_out), .turn(bcc_9_turn));
  ROM rom_1 (.addr({cdm_8_mark5_1_addr, I_Oadr}), .data(I_Odat), .sel(Code));
  RAM ram_1 (.addr({cdm_8_mark5_1_addr, I_Oadr}), .data(I_Odat), .sel(RAM), .clk(Cl), .ld(In_out_prime));  // open: clr

  // Other names for the same wires on the sheet: rd_wr_prime = In_out_prime; x = Player_selector

  // Notes on the sheet:
  //   data
  //   mem
  //   rd
  //   Аdr
endmodule

module MUX (
  input  [15:0] Input_0,
  input  sel,
  input  [15:0] Input_1,
  output [15:0] Output
);

  wire [15:0] and_1_out, and_2_out;
  wire [15:15] not_1_out;

  not not_1 (not_1_out[15], sel);
  assign and_1_out = Input_0 & {16{not_1_out[15]}};  // AND_Gate and_1, 16 bits wide
  assign and_2_out = {16{sel}} & Input_1;  // AND_Gate and_2, 16 bits wide
  assign Output = and_1_out | and_2_out;  // OR_Gate or_1, 16 bits wide
endmodule

module DM (
  input  Player,
  input  Turn,
  output [3:0] player_out,
  output [3:0] _1_out,
  output [3:0] _2_out,
  output [3:0] _3_out,
  output [3:0] _4_out
);

  wire and_1_out, and_2_out, x1;
  wire [15:0] not_1_out, not_2_out, register_1_q, x2;

  assign not_1_out = ~16'h9429;  // NOT_Gate not_1, 16 bits wide
  assign not_2_out = ~16'hf99f;  // NOT_Gate not_2, 16 bits wide
  MUX mux_1 (.Input_0(not_1_out), .sel(Player), .Input_1(not_2_out), .Output(x2));
  and and_1 (and_1_out, Turn, ~x1);  // AND_Gate
  Register #(.width(16)) register_1 (.D(x2), .Q(register_1_q), .clk(and_2_out));  // open: en, clr
  and and_2 (and_2_out, Turn, ~x1);  // AND_Gate
  Register #(.width(1)) register_2 (.D(Turn), .Q(x1), .clk(and_1_out));  // open: en, clr
  Pull_Resistor pull_resistor_1 (.node({_4_out, _3_out, _2_out, _1_out}));
  assign {_4_out, _3_out, _2_out, _1_out} = x1 ? ~register_1_q : 16'bz;  // Controlled_Inverter controlled_inverter_1

  assign player_out = _1_out;
endmodule

// WIN
module win (
  input  [3:0] _1_in,
  input  [3:0] _2_in,
  input  [3:0] _3_in,
  input  [3:0] _4_in,
  input  [3:0] _5_in,
  input  [3:0] _6_in,
  input  [3:0] _7_in,
  input  [3:0] _8_in,
  input  [3:0] _9_in,
  output O_win,
  output X_win,
  output Tie,
  output Trun_controll
);

  wire _1, _2, _3, _4, _5, _6, _7, _8, _9, and_1_out, and_2_out, and_3_out, and_4_out, and_14_out,
       and_15_out, and_16_out, and_17_out, and_18_out, and_19_out, and_20_out, and_21_out, and_22_out,
       and_23_out, and_24_out, and_25_out, and_26_out;

  and and_1 (and_1_out, _1_in[1], _2_in[1], _3_in[1]);
  and and_2 (and_2_out, _4_in[1], _5_in[1], _6_in[1]);
  and and_3 (and_3_out, _7_in[1], _8_in[1], _9_in[1]);
  and and_4 (and_4_out, _1_in[1], _4_in[1], _7_in[1]);
  and and_5 (_1, ~_1_in[1], _1_in[0]);  // AND_Gate
  and and_6 (_2, ~_2_in[1], _2_in[0]);  // AND_Gate
  and and_7 (_3, ~_3_in[1], _3_in[0]);  // AND_Gate
  and and_8 (_4, ~_4_in[1], _4_in[0]);  // AND_Gate
  and and_9 (_5, ~_5_in[1], _5_in[0]);  // AND_Gate
  and and_10 (_6, ~_6_in[1], _6_in[0]);  // AND_Gate
  and and_11 (_7, ~_7_in[1], _7_in[0]);  // AND_Gate
  and and_12 (_8, ~_8_in[1], _8_in[0]);  // AND_Gate
  and and_13 (_9, ~_9_in[1], _9_in[0]);  // AND_Gate
  and and_14 (and_14_out, _2_in[1], _5_in[1], _8_in[1]);
  and and_15 (and_15_out, _3_in[1], _6_in[1], _9_in[1]);
  and and_16 (and_16_out, _1_in[1], _5_in[1], _9_in[1]);
  and and_17 (and_17_out, _3_in[1], _5_in[1], _7_in[1]);
  or or_1 (O_win, and_1_out, and_2_out, and_3_out, and_4_out, and_14_out, and_15_out, and_16_out, and_17_out);
  and and_18 (and_18_out, _1, _2, _3);
  and and_19 (and_19_out, _4, _5, _6);
  and and_20 (and_20_out, _7, _8, _9);
  and and_21 (and_21_out, _1_in[0], _2_in[0], _3_in[0], _4_in[0], _5_in[0], _6_in[0], _7_in[0], _8_in[0], _9_in[0]);
  and and_22 (and_22_out, _1, _4, _7);
  and and_23 (and_23_out, _2, _5, _8);
  and and_24 (and_24_out, _3, _6, _9);
  or or_2 (Trun_controll, X_win, O_win, Tie);
  and and_25 (and_25_out, _1, _5, _9);
  and and_26 (and_26_out, _3, _5, _7);
  and and_27 (Tie, ~X_win, ~O_win, and_21_out);  // AND_Gate
  or or_3 (X_win, and_18_out, and_19_out, and_20_out, and_22_out, and_23_out, and_24_out, and_25_out, and_26_out);

  // Other names for the same wires on the sheet: _1v0 = _1_in[0]; _1v = _1_in[1]; _2v0 = _2_in[0]; _2v = _2_in[1];
  //   _3v0 = _3_in[0]; _3v = _3_in[1]; _4v0 = _4_in[0]; _4v = _4_in[1]; _5v0 = _5_in[0]; _5v = _5_in[1];
  //   _6v0 = _6_in[0]; _6v = _6_in[1]; _7v0 = _7_in[0]; _7v = _7_in[1]; _8v0 = _8_in[0]; _8v = _8_in[1];
  //   _9v0 = _9_in[0]; _9v = _9_in[1]

  // Notes on the sheet:
  //   O win horizont combination
  //   O vertical combination
  //   O diagonal combination
endmodule

module bcc (
  input  can_turn__0_can_1_can_t,
  input  btn,
  output turn
);

  Transistor transistor_1 (.in(btn), .out(turn), .gate(can_turn__0_can_1_can_t));
  Pull_Resistor pull_resistor_1 (.node(turn));
endmodule
